// Logisim project Assignment1.circ as structural Verilog: 11 circuits, main circuit main
module main (
  input  SetAlarm,
  input  OnOff,
  input  SetTime,
  input  PlusH,
  input  PlusM,
  input  Compare,
  output PM,
  output AM,
  output Hour1Bit1,
  output Hour1Bit2,
  output Hour1Bit3,
  output Hour1Bit4,
  output Hour2Bit1,
  output Hour2Bit2,
  output Hour2Bit3,
  output Min1Bit1,
  output Min1Bit2,
  output Min1Bit3,
  output Min1Bit4,
  output Min2Bit1,
  output Min2Bit2,
  output Min2Bit3,
  output Sec1Bit1,
  output Sec1Bit2,
  output Sec1Bit3,
  output Sec1Bit4,
  output Sec2Bit1,
  output Sec2Bit2,
  output Sec2Bit3,
  output Hour1Bit1Alarm,
  output Hour1Bit2Alarm,
  output Hour1Bit3Alarm,
  output Hour1Bit4Alarm,
  output Hour2Bit1Alarm,
  output Hour2Bit2Alarm,
  output Hour2Bit3Alarm,
  output Min1Bit1Alarm,
  output Min1Bit2Alarm,
  output Min1Bit3Alarm,
  output Min1Bit4Alarm,
  output Min2Bit1Alarm,
  output Min2Bit2Alarm,
  output Min2Bit3Alarm,
  output Sec1Bit1Alarm,
  output Sec1Bit2Alarm,
  output Sec1Bit3Alarm,
  output Sec1Bit4Alarm,
  output Sec2Bit1Alarm,
  output Sec2Bit2Alarm,
  output Sec2Bit3Alarm
);

  wire and_1_out, and_2_out, and_3_out, and_4_out, and_5_out, and_6_out, clock_1_out, clock_2_out,
       minutealarm_1_condition, minutes_1_condition, not_1_out, not_2_out, not_3_out, not_4_out, not_5_out,
       not_6_out, not_7_out, not_8_out, or_1_out, or_2_out, or_3_out, or_4_out, or_5_out, or_6_out, or_7_out,
       or_8_out, second_1_condition, secondalarm_1_condition;

  or or_1 (or_1_out, SetTime, SetAlarm);
  or or_2 (or_2_out, or_1_out, SetAlarm);
  not not_1 (not_1_out, or_3_out);
  or or_3 (or_3_out, and_1_out, minutes_1_condition);
  and and_1 (and_1_out, or_1_out, not_2_out, PlusH);
  not not_2 (not_2_out, SetAlarm);
  not not_3 (not_3_out, or_4_out);
  or or_4 (or_4_out, and_2_out, minutealarm_1_condition);
  and and_2 (and_2_out, or_2_out, PlusH);
  or or_5 (or_5_out, or_1_out, SetAlarm);
  Hours hours_1 (
    .OnOff(OnOff), .Clock(not_1_out), .Min1Bit1(Hour1Bit1), .Min1Bit2(Hour1Bit2), .Min1Bit3(Hour1Bit3),
    .Min1Bit4(Hour1Bit4), .Min2Bit1(Hour2Bit1), .Min2Bit2(Hour2Bit2), .Min2Bit3(Hour2Bit3), .PM(PM), .AM(AM));  // open: Condition
  HourAlarm houralarm_1 (
    .OnOff(OnOff), .Clock(not_3_out), .Min1Bit1(Hour1Bit1Alarm), .Min1Bit2(Hour1Bit2Alarm),
    .Min1Bit3(Hour1Bit3Alarm), .Min1Bit4(Hour1Bit4Alarm), .Min2Bit1(Hour2Bit1Alarm),
    .Min2Bit2(Hour2Bit2Alarm), .Min2Bit3(Hour2Bit3Alarm));  // open: Condition
  Clock clock_1 (.out(clock_1_out));
  or or_6 (or_6_out, or_1_out, SetAlarm);
  not not_4 (not_4_out, or_7_out);
  or or_7 (or_7_out, and_3_out, second_1_condition);
  and and_3 (and_3_out, or_1_out, not_5_out, PlusM);
  not not_5 (not_5_out, SetAlarm);
  not not_6 (not_6_out, or_5_out);
  not not_7 (not_7_out, or_8_out);
  or or_8 (or_8_out, and_4_out, secondalarm_1_condition);
  and and_4 (and_4_out, or_6_out, PlusM);
  and and_5 (and_5_out, Compare, clock_1_out, not_6_out);
  Minutes minutes_1 (
    .OnOff(OnOff), .Clock(not_4_out), .Min1Bit1(Min1Bit1), .Min1Bit2(Min1Bit2), .Min1Bit3(Min1Bit3),
    .Min1Bit4(Min1Bit4), .Min2Bit1(Min2Bit1), .Min2Bit2(Min2Bit2), .Min2Bit3(Min2Bit3),
    .Condition(minutes_1_condition));
  MinuteAlarm minutealarm_1 (
    .OnOff(OnOff), .Clock(not_7_out), .Min1Bit1(Min1Bit1Alarm), .Min1Bit2(Min1Bit2Alarm),
    .Min1Bit3(Min1Bit3Alarm), .Min1Bit4(Min1Bit4Alarm), .Min2Bit1(Min2Bit1Alarm), .Min2Bit2(Min2Bit2Alarm),
    .Min2Bit3(Min2Bit3Alarm), .Condition(minutealarm_1_condition));
  Clock clock_2 (.out(clock_2_out));
  not not_8 (not_8_out, or_1_out);
  and and_6 (and_6_out, clock_2_out, not_8_out);
  Second second_1 (
    .OnOff(OnOff), .Clock(and_6_out), .Min1Bit1(Sec1Bit1), .Min1Bit2(Sec1Bit2), .Min1Bit3(Sec1Bit3),
    .Min1Bit4(Sec1Bit4), .Min2Bit1(Sec2Bit1), .Min2Bit2(Sec2Bit2), .Min2Bit3(Sec2Bit3),
    .Condition(second_1_condition));
  SecondAlarm secondalarm_1 (
    .OnOff(OnOff), .Clock(and_5_out), .Min1Bit1(Sec1Bit1Alarm), .Min1Bit2(Sec1Bit2Alarm),
    .Min1Bit3(Sec1Bit3Alarm), .Min1Bit4(Sec1Bit4Alarm), .Min2Bit1(Sec2Bit1Alarm), .Min2Bit2(Sec2Bit2Alarm),
    .Min2Bit3(Sec2Bit3Alarm), .Condition(secondalarm_1_condition));
endmodule

module Second (
  input  OnOff,
  input  Clock,
  output Min1Bit1,
  output Min1Bit2,
  output Min1Bit3,
  output Min1Bit4,
  output Min2Bit1,
  output Min2Bit2,
  output Min2Bit3,
  output Condition
);

  wire and_1_out, and_2_out, and_3_out, and_5_out, and_6_out, and_7_out, j_k_ff_1_q, j_k_ff_2_q, j_k_ff_3_q,
       j_k_ff_4_q, j_k_ff_5_q, j_k_ff_6_q, j_k_ff_7_q, not_1_out, not_2_out, not_3_out;

  J_K_Flip_Flop #(.trigger("falling")) j_k_ff_1 (
    .J(OnOff), .K(OnOff), .clk(and_3_out), .Q(j_k_ff_1_q), .reset(and_2_out));  // open: Qn, preset
  D_Flip_Flop d_ff_1 (.D(j_k_ff_1_q), .clk(Clock), .Q(Min2Bit1));  // open: Qn, preset, reset
  J_K_Flip_Flop #(.trigger("falling")) j_k_ff_2 (
    .J(j_k_ff_1_q), .K(j_k_ff_1_q), .clk(and_3_out), .Q(j_k_ff_2_q), .reset(and_2_out));  // open: Qn, preset
  and and_1 (and_1_out, j_k_ff_1_q, j_k_ff_2_q);
  D_Flip_Flop d_ff_2 (.D(j_k_ff_2_q), .clk(Clock), .Q(Min2Bit2));  // open: Qn, preset, reset
  J_K_Flip_Flop #(.trigger("falling")) j_k_ff_3 (
    .J(and_1_out), .K(and_1_out), .clk(and_3_out), .Q(j_k_ff_3_q), .reset(and_2_out));  // open: Qn, preset
  D_Flip_Flop d_ff_3 (.D(j_k_ff_3_q), .clk(Clock), .Q(Min2Bit3));  // open: Qn, preset, reset
  and and_2 (and_2_out, j_k_ff_2_q, j_k_ff_3_q);
  not not_1 (not_1_out, Min1Bit2);
  not not_2 (not_2_out, Min1Bit3);
  and and_3 (and_3_out, j_k_ff_5_q, j_k_ff_7_q);
  not not_3 (not_3_out, Min2Bit2);
  and and_4 (Condition, Min1Bit1, not_1_out, not_2_out, Min1Bit4, Min2Bit1, Min2Bit3, not_3_out);
  J_K_Flip_Flop #(.trigger("falling")) j_k_ff_4 (
    .J(OnOff), .K(OnOff), .clk(Clock), .Q(j_k_ff_4_q), .reset(and_7_out));  // open: Qn, preset
  LED led_1 (.in(j_k_ff_4_q));
  D_Flip_Flop d_ff_4 (.D(j_k_ff_4_q), .clk(Clock), .Q(Min1Bit1));  // open: Qn, preset, reset
  J_K_Flip_Flop #(.trigger("falling")) j_k_ff_5 (
    .J(j_k_ff_4_q), .K(j_k_ff_4_q), .clk(Clock), .Q(j_k_ff_5_q), .reset(and_7_out));  // open: Qn, preset
  LED led_2 (.in(j_k_ff_5_q));
  and and_5 (and_5_out, j_k_ff_4_q, j_k_ff_5_q);
  J_K_Flip_Flop #(.trigger("falling")) j_k_ff_6 (
    .J(and_5_out), .K(and_5_out), .clk(Clock), .Q(j_k_ff_6_q), .reset(and_7_out));  // open: Qn, preset
  D_Flip_Flop d_ff_5 (.D(j_k_ff_5_q), .clk(Clock), .Q(Min1Bit2));  // open: Qn, preset, reset
  LED led_3 (.in(j_k_ff_6_q));
  and and_6 (and_6_out, and_5_out, j_k_ff_6_q);
  J_K_Flip_Flop #(.trigger("falling")) j_k_ff_7 (
    .J(and_6_out), .K(and_6_out), .clk(Clock), .Q(j_k_ff_7_q), .reset(and_7_out));  // open: Qn, preset
  D_Flip_Flop d_ff_6 (.D(j_k_ff_6_q), .clk(Clock), .Q(Min1Bit3));  // open: Qn, preset, reset
  LED led_4 (.in(j_k_ff_7_q));
  and and_7 (and_7_out, j_k_ff_5_q, j_k_ff_7_q);
  D_Flip_Flop d_ff_7 (.D(j_k_ff_7_q), .clk(Clock), .Q(Min1Bit4));  // open: Qn, preset, reset

  // Notes on the sheet:
  //   Min 2
  //   Min 1
endmodule

module Minutes (
  input  OnOff,
  input  Clock,
  output Min1Bit1,
  output Min1Bit2,
  output Min1Bit3,
  output Min1Bit4,
  output Min2Bit1,
  output Min2Bit2,
  output Min2Bit3,
  output Condition
);

  wire and_1_out, and_2_out, and_3_out, and_5_out, and_6_out, and_7_out, j_k_ff_1_q, j_k_ff_2_q, j_k_ff_3_q,
       j_k_ff_4_q, j_k_ff_5_q, j_k_ff_6_q, j_k_ff_7_q, not_1_out, not_2_out, not_3_out;

  J_K_Flip_Flop #(.trigger("falling")) j_k_ff_1 (
    .J(OnOff), .K(OnOff), .clk(and_3_out), .Q(j_k_ff_1_q), .reset(and_2_out));  // open: Qn, preset
  D_Flip_Flop d_ff_1 (.D(j_k_ff_1_q), .clk(Clock), .Q(Min2Bit1));  // open: Qn, preset, reset
  J_K_Flip_Flop #(.trigger("falling")) j_k_ff_2 (
    .J(j_k_ff_1_q), .K(j_k_ff_1_q), .clk(and_3_out), .Q(j_k_ff_2_q), .reset(and_2_out));  // open: Qn, preset
  and and_1 (and_1_out, j_k_ff_1_q, j_k_ff_2_q);
  D_Flip_Flop d_ff_2 (.D(j_k_ff_2_q), .clk(Clock), .Q(Min2Bit2));  // open: Qn, preset, reset
  J_K_Flip_Flop #(.trigger("falling")) j_k_ff_3 (
    .J(and_1_out), .K(and_1_out), .clk(and_3_out), .Q(j_k_ff_3_q), .reset(and_2_out));  // open: Qn, preset
  D_Flip_Flop d_ff_3 (.D(j_k_ff_3_q), .clk(Clock), .Q(Min2Bit3));  // open: Qn, preset, reset
  and and_2 (and_2_out, j_k_ff_2_q, j_k_ff_3_q);
  not not_1 (not_1_out, Min1Bit2);
  not not_2 (not_2_out, Min1Bit3);
  and and_3 (and_3_out, j_k_ff_5_q, j_k_ff_7_q);
  not not_3 (not_3_out, Min2Bit2);
  and and_4 (Condition, Min1Bit1, not_1_out, not_2_out, Min1Bit4, Min2Bit1, Min2Bit3, not_3_out);
  J_K_Flip_Flop #(.trigger("falling")) j_k_ff_4 (
    .J(OnOff), .K(OnOff), .clk(Clock), .Q(j_k_ff_4_q), .reset(and_7_out));  // open: Qn, preset
  LED led_1 (.in(j_k_ff_4_q));
  D_Flip_Flop d_ff_4 (.D(j_k_ff_4_q), .clk(Clock), .Q(Min1Bit1));  // open: Qn, preset, reset
  J_K_Flip_Flop #(.trigger("falling")) j_k_ff_5 (
    .J(j_k_ff_4_q), .K(j_k_ff_4_q), .clk(Clock), .Q(j_k_ff_5_q), .reset(and_7_out));  // open: Qn, preset
  LED led_2 (.in(j_k_ff_5_q));
  and and_5 (and_5_out, j_k_ff_4_q, j_k_ff_5_q);
  J_K_Flip_Flop #(.trigger("falling")) j_k_ff_6 (
    .J(and_5_out), .K(and_5_out), .clk(Clock), .Q(j_k_ff_6_q), .reset(and_7_out));  // open: Qn, preset
  D_Flip_Flop d_ff_5 (.D(j_k_ff_5_q), .clk(Clock), .Q(Min1Bit2));  // open: Qn, preset, reset
  LED led_3 (.in(j_k_ff_6_q));
  and and_6 (and_6_out, and_5_out, j_k_ff_6_q);
  J_K_Flip_Flop #(.trigger("falling")) j_k_ff_7 (
    .J(and_6_out), .K(and_6_out), .clk(Clock), .Q(j_k_ff_7_q), .reset(and_7_out));  // open: Qn, preset
  D_Flip_Flop d_ff_6 (.D(j_k_ff_6_q), .clk(Clock), .Q(Min1Bit3));  // open: Qn, preset, reset
  LED led_4 (.in(j_k_ff_7_q));
  and and_7 (and_7_out, j_k_ff_5_q, j_k_ff_7_q);
  D_Flip_Flop d_ff_7 (.D(j_k_ff_7_q), .clk(Clock), .Q(Min1Bit4));  // open: Qn, preset, reset

  // Notes on the sheet:
  //   Min 2
  //   Min 1
endmodule

module Hours (
  input  OnOff,
  input  Clock,
  output Min1Bit1,
  output Min1Bit2,
  output Min1Bit3,
  output Min1Bit4,
  output Min2Bit1,
  output Min2Bit2,
  output Min2Bit3,
  output Condition,
  output PM,
  output AM
);

  wire and_1_out, and_2_out, and_3_out, and_4_out, and_5_out, and_6_out, d_ff_4_qn, j_k_ff_1_q, j_k_ff_2_q,
       j_k_ff_3_q, j_k_ff_4_q, j_k_ff_5_q, j_k_ff_6_q, j_k_ff_7_q, not_1_out, not_2_out, not_4_out,
       not_5_out, not_6_out, or_1_out;

  J_K_Flip_Flop #(.trigger("falling")) j_k_ff_1 (
    .J(OnOff), .K(OnOff), .clk(and_2_out), .Q(j_k_ff_1_q), .reset(and_3_out));  // open: Qn, preset
  D_Flip_Flop d_ff_1 (.D(j_k_ff_1_q), .clk(Clock), .Q(Min2Bit1));  // open: Qn, preset, reset
  J_K_Flip_Flop #(.trigger("falling")) j_k_ff_2 (
    .J(j_k_ff_1_q), .K(j_k_ff_1_q), .clk(and_2_out), .Q(j_k_ff_2_q), .reset(and_3_out));  // open: Qn, preset
  and and_1 (and_1_out, j_k_ff_1_q, j_k_ff_2_q);
  D_Flip_Flop d_ff_2 (.D(j_k_ff_2_q), .clk(Clock), .Q(Min2Bit2));  // open: Qn, preset, reset
  J_K_Flip_Flop #(.trigger("falling")) j_k_ff_3 (
    .J(and_1_out), .K(and_1_out), .clk(and_2_out), .Q(j_k_ff_3_q), .reset(and_3_out));  // open: Qn, preset
  D_Flip_Flop d_ff_3 (.D(j_k_ff_3_q), .clk(Clock), .Q(Min2Bit3));  // open: Qn, preset, reset
  D_Flip_Flop d_ff_4 (.D(d_ff_4_qn), .clk(and_3_out), .Q(PM), .Qn(d_ff_4_qn));  // open: preset, reset
  not not_1 (not_1_out, Min1Bit1);
  not not_2 (not_2_out, Min1Bit3);
  not not_3 (AM, PM);
  and and_2 (and_2_out, j_k_ff_5_q, j_k_ff_7_q);
  not not_4 (not_4_out, Min1Bit4);
  not not_5 (not_5_out, Min2Bit2);
  not not_6 (not_6_out, Min2Bit3);
  and and_3 (and_3_out, not_1_out, Min1Bit2, not_2_out, not_4_out, Min2Bit1, not_5_out, not_6_out);
  not not_7 (Condition, and_3_out);
  J_K_Flip_Flop #(.trigger("falling")) j_k_ff_4 (
    .J(OnOff), .K(OnOff), .clk(Clock), .Q(j_k_ff_4_q));  // open: Qn, preset, reset
  LED led_1 (.in(j_k_ff_4_q));
  D_Flip_Flop d_ff_5 (.D(j_k_ff_4_q), .clk(Clock), .Q(Min1Bit1));  // open: Qn, preset, reset
  J_K_Flip_Flop #(.trigger("falling")) j_k_ff_5 (
    .J(j_k_ff_4_q), .K(j_k_ff_4_q), .clk(Clock), .Q(j_k_ff_5_q), .reset(or_1_out));  // open: Qn, preset
  LED led_2 (.in(j_k_ff_5_q));
  and and_4 (and_4_out, j_k_ff_4_q, j_k_ff_5_q);
  J_K_Flip_Flop #(.trigger("falling")) j_k_ff_6 (
    .J(and_4_out), .K(and_4_out), .clk(Clock), .Q(j_k_ff_6_q), .reset(or_1_out));  // open: Qn, preset
  D_Flip_Flop d_ff_6 (.D(j_k_ff_5_q), .clk(Clock), .Q(Min1Bit2));  // open: Qn, preset, reset
  LED led_3 (.in(j_k_ff_6_q));
  and and_5 (and_5_out, and_4_out, j_k_ff_6_q);
  J_K_Flip_Flop #(.trigger("falling")) j_k_ff_7 (
    .J(and_5_out), .K(and_5_out), .clk(Clock), .Q(j_k_ff_7_q), .reset(or_1_out));  // open: Qn, preset
  D_Flip_Flop d_ff_7 (.D(j_k_ff_6_q), .clk(Clock), .Q(Min1Bit3));  // open: Qn, preset, reset
  LED led_4 (.in(j_k_ff_7_q));
  and and_6 (and_6_out, j_k_ff_5_q, j_k_ff_7_q);
  or or_1 (or_1_out, and_6_out, and_3_out);
  D_Flip_Flop d_ff_8 (.D(j_k_ff_7_q), .clk(Clock), .Q(Min1Bit4));  // open: Qn, preset, reset

  // Notes on the sheet:
  //   Min 1
endmodule

module SecondAlarm (
  input  OnOff,
  input  Clock,
  output Min1Bit1,
  output Min1Bit2,
  output Min1Bit3,
  output Min1Bit4,
  output Min2Bit1,
  output Min2Bit2,
  output Min2Bit3,
  output Condition
);

  wire and_1_out, and_2_out, and_3_out, and_5_out, and_6_out, and_7_out, j_k_ff_1_q, j_k_ff_2_q, j_k_ff_3_q,
       j_k_ff_4_q, j_k_ff_5_q, j_k_ff_6_q, j_k_ff_7_q, not_1_out, not_2_out, not_3_out;

  J_K_Flip_Flop #(.trigger("falling")) j_k_ff_1 (
    .J(OnOff), .K(OnOff), .clk(and_3_out), .Q(j_k_ff_1_q), .reset(and_2_out));  // open: Qn, preset
  D_Flip_Flop d_ff_1 (.D(j_k_ff_1_q), .clk(Clock), .Q(Min2Bit1));  // open: Qn, preset, reset
  J_K_Flip_Flop #(.trigger("falling")) j_k_ff_2 (
    .J(j_k_ff_1_q), .K(j_k_ff_1_q), .clk(and_3_out), .Q(j_k_ff_2_q), .reset(and_2_out));  // open: Qn, preset
  and and_1 (and_1_out, j_k_ff_1_q, j_k_ff_2_q);
  D_Flip_Flop d_ff_2 (.D(j_k_ff_2_q), .clk(Clock), .Q(Min2Bit2));  // open: Qn, preset, reset
  J_K_Flip_Flop #(.trigger("falling")) j_k_ff_3 (
    .J(and_1_out), .K(and_1_out), .clk(and_3_out), .Q(j_k_ff_3_q), .reset(and_2_out));  // open: Qn, preset
  D_Flip_Flop d_ff_3 (.D(j_k_ff_3_q), .clk(Clock), .Q(Min2Bit3));  // open: Qn, preset, reset
  and and_2 (and_2_out, j_k_ff_2_q, j_k_ff_3_q);
  not not_1 (not_1_out, Min1Bit2);
  not not_2 (not_2_out, Min1Bit3);
  and and_3 (and_3_out, j_k_ff_5_q, j_k_ff_7_q);
  not not_3 (not_3_out, Min2Bit2);
  and and_4 (Condition, Min1Bit1, not_1_out, not_2_out, Min1Bit4, Min2Bit1, Min2Bit3, not_3_out);
  J_K_Flip_Flop #(.trigger("falling")) j_k_ff_4 (
    .J(OnOff), .K(OnOff), .clk(Clock), .Q(j_k_ff_4_q), .reset(and_7_out));  // open: Qn, preset
  LED led_1 (.in(j_k_ff_4_q));
  D_Flip_Flop d_ff_4 (.D(j_k_ff_4_q), .clk(Clock), .Q(Min1Bit1));  // open: Qn, preset, reset
  J_K_Flip_Flop #(.trigger("falling")) j_k_ff_5 (
    .J(j_k_ff_4_q), .K(j_k_ff_4_q), .clk(Clock), .Q(j_k_ff_5_q), .reset(and_7_out));  // open: Qn, preset
  LED led_2 (.in(j_k_ff_5_q));
  and and_5 (and_5_out, j_k_ff_4_q, j_k_ff_5_q);
  J_K_Flip_Flop #(.trigger("falling")) j_k_ff_6 (
    .J(and_5_out), .K(and_5_out), .clk(Clock), .Q(j_k_ff_6_q), .reset(and_7_out));  // open: Qn, preset
  D_Flip_Flop d_ff_5 (.D(j_k_ff_5_q), .clk(Clock), .Q(Min1Bit2));  // open: Qn, preset, reset
  LED led_3 (.in(j_k_ff_6_q));
  and and_6 (and_6_out, and_5_out, j_k_ff_6_q);
  J_K_Flip_Flop #(.trigger("falling")) j_k_ff_7 (
    .J(and_6_out), .K(and_6_out), .clk(Clock), .Q(j_k_ff_7_q), .reset(and_7_out));  // open: Qn, preset
  D_Flip_Flop d_ff_6 (.D(j_k_ff_6_q), .clk(Clock), .Q(Min1Bit3));  // open: Qn, preset, reset
  LED led_4 (.in(j_k_ff_7_q));
  and and_7 (and_7_out, j_k_ff_5_q, j_k_ff_7_q);
  D_Flip_Flop d_ff_7 (.D(j_k_ff_7_q), .clk(Clock), .Q(Min1Bit4));  // open: Qn, preset, reset

  // Notes on the sheet:
  //   Min 2
  //   Min 1
endmodule

module MinuteAlarm (
  input  OnOff,
  input  Clock,
  output Min1Bit1,
  output Min1Bit2,
  output Min1Bit3,
  output Min1Bit4,
  output Min2Bit1,
  output Min2Bit2,
  output Min2Bit3,
  output Condition
);

  wire and_1_out, and_2_out, and_3_out, and_5_out, and_6_out, and_7_out, j_k_ff_1_q, j_k_ff_2_q, j_k_ff_3_q,
       j_k_ff_4_q, j_k_ff_5_q, j_k_ff_6_q, j_k_ff_7_q, not_1_out, not_2_out, not_3_out;

  J_K_Flip_Flop #(.trigger("falling")) j_k_ff_1 (
    .J(OnOff), .K(OnOff), .clk(and_3_out), .Q(j_k_ff_1_q), .reset(and_2_out));  // open: Qn, preset
  D_Flip_Flop d_ff_1 (.D(j_k_ff_1_q), .clk(Clock), .Q(Min2Bit1));  // open: Qn, preset, reset
  J_K_Flip_Flop #(.trigger("falling")) j_k_ff_2 (
    .J(j_k_ff_1_q), .K(j_k_ff_1_q), .clk(and_3_out), .Q(j_k_ff_2_q), .reset(and_2_out));  // open: Qn, preset
  and and_1 (and_1_out, j_k_ff_1_q, j_k_ff_2_q);
  D_Flip_Flop d_ff_2 (.D(j_k_ff_2_q), .clk(Clock), .Q(Min2Bit2));  // open: Qn, preset, reset
  J_K_Flip_Flop #(.trigger("falling")) j_k_ff_3 (
    .J(and_1_out), .K(and_1_out), .clk(and_3_out), .Q(j_k_ff_3_q), .reset(and_2_out));  // open: Qn, preset
  D_Flip_Flop d_ff_3 (.D(j_k_ff_3_q), .clk(Clock), .Q(Min2Bit3));  // open: Qn, preset, reset
  and and_2 (and_2_out, j_k_ff_2_q, j_k_ff_3_q);
  not not_1 (not_1_out, Min1Bit2);
  not not_2 (not_2_out, Min1Bit3);
  and and_3 (and_3_out, j_k_ff_5_q, j_k_ff_7_q);
  not not_3 (not_3_out, Min2Bit2);
  and and_4 (Condition, Min1Bit1, not_1_out, not_2_out, Min1Bit4, Min2Bit1, Min2Bit3, not_3_out);
  J_K_Flip_Flop #(.trigger("falling")) j_k_ff_4 (
    .J(OnOff), .K(OnOff), .clk(Clock), .Q(j_k_ff_4_q), .reset(and_7_out));  // open: Qn, preset
  D_Flip_Flop d_ff_4 (.D(j_k_ff_4_q), .clk(Clock), .Q(Min1Bit1));  // open: Qn, preset, reset
  J_K_Flip_Flop #(.trigger("falling")) j_k_ff_5 (
    .J(j_k_ff_4_q), .K(j_k_ff_4_q), .clk(Clock), .Q(j_k_ff_5_q), .reset(and_7_out));  // open: Qn, preset
  and and_5 (and_5_out, j_k_ff_4_q, j_k_ff_5_q);
  D_Flip_Flop d_ff_5 (.D(j_k_ff_5_q), .clk(Clock), .Q(Min1Bit2));  // open: Qn, preset, reset
  J_K_Flip_Flop #(.trigger("falling")) j_k_ff_6 (
    .J(and_5_out), .K(and_5_out), .clk(Clock), .Q(j_k_ff_6_q), .reset(and_7_out));  // open: Qn, preset
  D_Flip_Flop d_ff_6 (.D(j_k_ff_6_q), .clk(Clock), .Q(Min1Bit3));  // open: Qn, preset, reset
  and and_6 (and_6_out, and_5_out, j_k_ff_6_q);
  J_K_Flip_Flop #(.trigger("falling")) j_k_ff_7 (
    .J(and_6_out), .K(and_6_out), .clk(Clock), .Q(j_k_ff_7_q), .reset(and_7_out));  // open: Qn, preset
  and and_7 (and_7_out, j_k_ff_5_q, j_k_ff_7_q);
  D_Flip_Flop d_ff_7 (.D(j_k_ff_7_q), .clk(Clock), .Q(Min1Bit4));  // open: Qn, preset, reset

  // Notes on the sheet:
  //   Min 2
  //   Min 1
endmodule

module HourAlarm (
  input  OnOff,
  input  Clock,
  output Min1Bit1,
  output Min1Bit2,
  output Min1Bit3,
  output Min1Bit4,
  output Min2Bit1,
  output Min2Bit2,
  output Min2Bit3,
  output Condition
);

  wire and_1_out, and_2_out, and_3_out, and_4_out, and_5_out, and_6_out, j_k_ff_1_q, j_k_ff_2_q, j_k_ff_3_q,
       j_k_ff_4_q, j_k_ff_5_q, j_k_ff_6_q, j_k_ff_7_q, not_1_out, not_2_out, not_3_out, not_4_out, not_5_out,
       or_1_out;

  J_K_Flip_Flop #(.trigger("falling")) j_k_ff_1 (
    .J(OnOff), .K(OnOff), .clk(and_2_out), .Q(j_k_ff_1_q), .reset(and_3_out));  // open: Qn, preset
  D_Flip_Flop d_ff_1 (.D(j_k_ff_1_q), .clk(Clock), .Q(Min2Bit1));  // open: Qn, preset, reset
  J_K_Flip_Flop #(.trigger("falling")) j_k_ff_2 (
    .J(j_k_ff_1_q), .K(j_k_ff_1_q), .clk(and_2_out), .Q(j_k_ff_2_q), .reset(and_3_out));  // open: Qn, preset
  and and_1 (and_1_out, j_k_ff_1_q, j_k_ff_2_q);
  D_Flip_Flop d_ff_2 (.D(j_k_ff_2_q), .clk(Clock), .Q(Min2Bit2));  // open: Qn, preset, reset
  J_K_Flip_Flop #(.trigger("falling")) j_k_ff_3 (
    .J(and_1_out), .K(and_1_out), .clk(and_2_out), .Q(j_k_ff_3_q), .reset(and_3_out));  // open: Qn, preset
  D_Flip_Flop d_ff_3 (.D(j_k_ff_3_q), .clk(Clock), .Q(Min2Bit3));  // open: Qn, preset, reset
  not not_1 (not_1_out, Min1Bit1);
  not not_2 (not_2_out, Min1Bit3);
  and and_2 (and_2_out, j_k_ff_5_q, j_k_ff_7_q);
  not not_3 (not_3_out, Min1Bit4);
  not not_4 (not_4_out, Min2Bit3);
  not not_5 (not_5_out, Min2Bit2);
  and and_3 (and_3_out, not_1_out, Min1Bit2, not_2_out, not_3_out, Min2Bit1, not_4_out, not_5_out);
  not not_6 (Condition, and_3_out);
  J_K_Flip_Flop #(.trigger("falling")) j_k_ff_4 (
    .J(OnOff), .K(OnOff), .clk(Clock), .Q(j_k_ff_4_q));  // open: Qn, preset, reset
  LED led_1 (.in(j_k_ff_4_q));
  D_Flip_Flop d_ff_4 (.D(j_k_ff_4_q), .clk(Clock), .Q(Min1Bit1));  // open: Qn, preset, reset
  J_K_Flip_Flop #(.trigger("falling")) j_k_ff_5 (
    .J(j_k_ff_4_q), .K(j_k_ff_4_q), .clk(Clock), .Q(j_k_ff_5_q), .reset(or_1_out));  // open: Qn, preset
  LED led_2 (.in(j_k_ff_5_q));
  and and_4 (and_4_out, j_k_ff_4_q, j_k_ff_5_q);
  J_K_Flip_Flop #(.trigger("falling")) j_k_ff_6 (
    .J(and_4_out), .K(and_4_out), .clk(Clock), .Q(j_k_ff_6_q), .reset(or_1_out));  // open: Qn, preset
  D_Flip_Flop d_ff_5 (.D(j_k_ff_5_q), .clk(Clock), .Q(Min1Bit2));  // open: Qn, preset, reset
  LED led_3 (.in(j_k_ff_6_q));
  and and_5 (and_5_out, and_4_out, j_k_ff_6_q);
  J_K_Flip_Flop #(.trigger("falling")) j_k_ff_7 (
    .J(and_5_out), .K(and_5_out), .clk(Clock), .Q(j_k_ff_7_q), .reset(or_1_out));  // open: Qn, preset
  D_Flip_Flop d_ff_6 (.D(j_k_ff_6_q), .clk(Clock), .Q(Min1Bit3));  // open: Qn, preset, reset
  LED led_4 (.in(j_k_ff_7_q));
  and and_6 (and_6_out, j_k_ff_5_q, j_k_ff_7_q);
  or or_1 (or_1_out, and_6_out, and_3_out);
  D_Flip_Flop d_ff_7 (.D(j_k_ff_7_q), .clk(Clock), .Q(Min1Bit4));  // open: Qn, preset, reset

  // Notes on the sheet:
  //   Min 1
endmodule

module Compare (
  input  bit1,
  input  in_2,
  input  bit2,
  input  in_4,
  input  bit3,
  input  in_6,
  input  bit4,
  input  in_8,
  input  SecondBit1,
  input  in_10,
  input  SecondBit2,
  input  in_12,
  input  SecondBit3,
  input  in_14,
  output out_15
);

  wire xnor_1_out, xnor_2_out, xnor_3_out, xnor_4_out, xnor_5_out, xnor_6_out, xnor_7_out;

  xnor xnor_1 (xnor_1_out, bit1, in_2);
  xnor xnor_2 (xnor_2_out, bit2, in_4);
  xnor xnor_3 (xnor_3_out, bit3, in_6);
  xnor xnor_4 (xnor_4_out, bit4, in_8);
  xnor xnor_5 (xnor_5_out, SecondBit1, in_10);
  xnor xnor_6 (xnor_6_out, SecondBit2, in_12);
  xnor xnor_7 (xnor_7_out, SecondBit3, in_14);
  and and_1 (out_15, xnor_1_out, xnor_2_out, xnor_3_out, xnor_4_out, xnor_5_out, xnor_6_out, xnor_7_out);
endmodule

module CLockDisplay (
  input  SetTime,
  input  SetAlarm,
  input  OnOff,
  input  OnOffAlarm,
  input  in_5,
  input  in_6
);

  wire and_1_out, and_2_out, clock_1_out, compare_1_out_15, compare_2_out_15, compare_3_out_15, d_ff_1_q,
       main_1_am, main_1_hour1bit1, main_1_hour1bit1alarm, main_1_hour1bit2, main_1_hour1bit2alarm,
       main_1_hour1bit3, main_1_hour1bit3alarm, main_1_hour1bit4, main_1_hour1bit4alarm, main_1_hour2bit1,
       main_1_hour2bit1alarm, main_1_hour2bit2, main_1_hour2bit2alarm, main_1_hour2bit3,
       main_1_hour2bit3alarm, main_1_min1bit1, main_1_min1bit1alarm, main_1_min1bit2, main_1_min1bit2alarm,
       main_1_min1bit3, main_1_min1bit3alarm, main_1_min1bit4, main_1_min1bit4alarm, main_1_min2bit1,
       main_1_min2bit1alarm, main_1_min2bit2, main_1_min2bit2alarm, main_1_min2bit3, main_1_min2bit3alarm,
       main_1_pm, main_1_sec1bit1, main_1_sec1bit1alarm, main_1_sec1bit2, main_1_sec1bit2alarm,
       main_1_sec1bit3, main_1_sec1bit3alarm, main_1_sec1bit4, main_1_sec1bit4alarm, main_1_sec2bit1,
       main_1_sec2bit1alarm, main_1_sec2bit2, main_1_sec2bit2alarm, main_1_sec2bit3, main_1_sec2bit3alarm,
       PlusH_out, PlusM_out;
  wire [2:0] totalswitchclock_1_out_20, totalswitchclock_2_out_20;
  wire [3:0] totalswitchclock_1_out_16, totalswitchclock_2_out_16;

  Hex_Digit_Display hex_digit_display_1 (.value({in_6, totalswitchclock_1_out_20}));  // open: dp
  Hex_Digit_Display hex_digit_display_2 (.value(totalswitchclock_1_out_16));  // open: dp
  Hex_Digit_Display hex_digit_display_3 (.value({in_5, totalswitchclock_2_out_20}));  // open: dp
  Hex_Digit_Display hex_digit_display_4 (.value(totalswitchclock_2_out_16));  // open: dp
  LED Alarm (.in(and_1_out));
  and and_1 (and_1_out, OnOffAlarm, and_2_out);
  Button PlusH (.out(PlusH_out));
  Button PlusM (.out(PlusM_out));
  LED PM (.in(main_1_pm));
  LED AM (.in(main_1_am));
  D_Flip_Flop d_ff_1 (.D(and_2_out), .clk(clock_1_out), .Q(d_ff_1_q));  // open: Qn, preset, reset
  Clock clock_1 (.out(clock_1_out));
  main main_1 (
    .PM(main_1_pm), .AM(main_1_am), .PlusH(PlusH_out), .PlusM(PlusM_out), .Compare(d_ff_1_q),
    .SetTime(SetTime), .SetAlarm(SetAlarm), .OnOff(OnOff), .Hour1Bit1(main_1_hour1bit1),
    .Hour1Bit2(main_1_hour1bit2), .Hour1Bit3(main_1_hour1bit3), .Hour1Bit4(main_1_hour1bit4),
    .Hour2Bit1(main_1_hour2bit1), .Hour2Bit2(main_1_hour2bit2), .Hour2Bit3(main_1_hour2bit3),
    .Min1Bit1(main_1_min1bit1), .Min1Bit2(main_1_min1bit2), .Min1Bit3(main_1_min1bit3),
    .Min1Bit4(main_1_min1bit4), .Min2Bit1(main_1_min2bit1), .Min2Bit2(main_1_min2bit2),
    .Min2Bit3(main_1_min2bit3), .Sec1Bit1(main_1_sec1bit1), .Sec1Bit2(main_1_sec1bit2),
    .Sec1Bit3(main_1_sec1bit3), .Sec1Bit4(main_1_sec1bit4), .Sec2Bit1(main_1_sec2bit1),
    .Sec2Bit2(main_1_sec2bit2), .Sec2Bit3(main_1_sec2bit3), .Hour1Bit1Alarm(main_1_hour1bit1alarm),
    .Hour1Bit2Alarm(main_1_hour1bit2alarm), .Hour1Bit3Alarm(main_1_hour1bit3alarm),
    .Hour1Bit4Alarm(main_1_hour1bit4alarm), .Hour2Bit1Alarm(main_1_hour2bit1alarm),
    .Hour2Bit2Alarm(main_1_hour2bit2alarm), .Hour2Bit3Alarm(main_1_hour2bit3alarm),
    .Min1Bit1Alarm(main_1_min1bit1alarm), .Min1Bit2Alarm(main_1_min1bit2alarm),
    .Min1Bit3Alarm(main_1_min1bit3alarm), .Min1Bit4Alarm(main_1_min1bit4alarm),
    .Min2Bit1Alarm(main_1_min2bit1alarm), .Min2Bit2Alarm(main_1_min2bit2alarm),
    .Min2Bit3Alarm(main_1_min2bit3alarm), .Sec1Bit1Alarm(main_1_sec1bit1alarm),
    .Sec1Bit2Alarm(main_1_sec1bit2alarm), .Sec1Bit3Alarm(main_1_sec1bit3alarm),
    .Sec1Bit4Alarm(main_1_sec1bit4alarm), .Sec2Bit1Alarm(main_1_sec2bit1alarm),
    .Sec2Bit2Alarm(main_1_sec2bit2alarm), .Sec2Bit3Alarm(main_1_sec2bit3alarm));
  Compare compare_1 (
    .bit1(main_1_hour1bit1), .in_2(main_1_hour1bit1alarm), .bit2(main_1_hour1bit2),
    .in_4(main_1_hour1bit2alarm), .bit3(main_1_hour1bit3), .in_6(main_1_hour1bit3alarm),
    .bit4(main_1_hour1bit4), .in_8(main_1_hour1bit4alarm), .SecondBit1(main_1_hour2bit1),
    .in_10(main_1_hour2bit1alarm), .SecondBit2(main_1_hour2bit2), .in_12(main_1_hour2bit2alarm),
    .SecondBit3(main_1_hour2bit3), .in_14(main_1_hour2bit3alarm), .out_15(compare_1_out_15));
  Compare compare_2 (
    .bit1(main_1_min1bit1), .in_2(main_1_min1bit1alarm), .bit2(main_1_min1bit2), .in_4(main_1_min1bit2alarm),
    .bit3(main_1_min1bit3), .in_6(main_1_min1bit3alarm), .bit4(main_1_min1bit4), .in_8(main_1_min1bit4alarm),
    .SecondBit1(main_1_min2bit1), .in_10(main_1_min2bit1alarm), .SecondBit2(main_1_min2bit2),
    .in_12(main_1_min2bit2alarm), .SecondBit3(main_1_min2bit3), .in_14(main_1_min2bit3alarm),
    .out_15(compare_2_out_15));
  Compare compare_3 (
    .bit1(main_1_sec1bit1), .in_2(main_1_sec1bit1alarm), .bit2(main_1_sec1bit2), .in_4(main_1_sec1bit2alarm),
    .bit3(main_1_sec1bit3), .in_6(main_1_sec1bit3alarm), .bit4(main_1_sec1bit4), .in_8(main_1_sec1bit4alarm),
    .SecondBit1(main_1_sec2bit1), .in_10(main_1_sec2bit1alarm), .SecondBit2(main_1_sec2bit2),
    .in_12(main_1_sec2bit2alarm), .SecondBit3(main_1_sec2bit3), .in_14(main_1_sec2bit3alarm),
    .out_15(compare_3_out_15));
  and and_2 (and_2_out, compare_1_out_15, compare_2_out_15, compare_3_out_15);
  TotalSwitchClock totalswitchclock_1 (
    .OnOff(SetAlarm), .Bit1(main_1_hour1bit1), .Bit2(main_1_hour1bit2), .Bit3(main_1_hour1bit3),
    .Bit4(main_1_hour1bit4), .SecondBit1(main_1_hour2bit1), .SecondBit2(main_1_hour2bit2),
    .SecondBit3(main_1_hour2bit3), .Bit1Alarm(main_1_hour1bit1alarm), .Bit2Alarm(main_1_hour1bit2alarm),
    .Bit3Alarm(main_1_hour1bit3alarm), .Bit4Alarm(main_1_hour1bit4alarm),
    .SecondBit1Alarm(main_1_hour2bit1alarm), .SecondBit2Alarm(main_1_hour2bit2alarm),
    .SecondBit3Alarm(main_1_hour2bit3alarm), .out_16(totalswitchclock_1_out_16[0]),
    .out_17(totalswitchclock_1_out_16[1]), .out_18(totalswitchclock_1_out_16[2]),
    .out_19(totalswitchclock_1_out_16[3]), .out_20(totalswitchclock_1_out_20[0]),
    .out_21(totalswitchclock_1_out_20[1]), .out_22(totalswitchclock_1_out_20[2]));
  TotalSwitchClock totalswitchclock_2 (
    .OnOff(SetAlarm), .Bit1(main_1_min1bit1), .Bit2(main_1_min1bit2), .Bit3(main_1_min1bit3),
    .Bit4(main_1_min1bit4), .SecondBit1(main_1_min2bit1), .SecondBit2(main_1_min2bit2),
    .SecondBit3(main_1_min2bit3), .Bit1Alarm(main_1_min1bit1alarm), .Bit2Alarm(main_1_min1bit2alarm),
    .Bit3Alarm(main_1_min1bit3alarm), .Bit4Alarm(main_1_min1bit4alarm),
    .SecondBit1Alarm(main_1_min2bit1alarm), .SecondBit2Alarm(main_1_min2bit2alarm),
    .SecondBit3Alarm(main_1_min2bit3alarm), .out_16(totalswitchclock_2_out_16[0]),
    .out_17(totalswitchclock_2_out_16[1]), .out_18(totalswitchclock_2_out_16[2]),
    .out_19(totalswitchclock_2_out_16[3]), .out_20(totalswitchclock_2_out_20[0]),
    .out_21(totalswitchclock_2_out_20[1]), .out_22(totalswitchclock_2_out_20[2]));
  TotalSwitchClock totalswitchclock_3 (
    .OnOff(SetAlarm), .Bit1(main_1_sec1bit1), .Bit2(main_1_sec1bit2), .Bit3(main_1_sec1bit3),
    .Bit4(main_1_sec1bit4), .SecondBit1(main_1_sec2bit1), .SecondBit2(main_1_sec2bit2),
    .SecondBit3(main_1_sec2bit3), .Bit1Alarm(main_1_sec1bit1alarm), .Bit2Alarm(main_1_sec1bit2alarm),
    .Bit3Alarm(main_1_sec1bit3alarm), .Bit4Alarm(main_1_sec1bit4alarm),
    .SecondBit1Alarm(main_1_sec2bit1alarm), .SecondBit2Alarm(main_1_sec2bit2alarm),
    .SecondBit3Alarm(main_1_sec2bit3alarm));  // open: out_16, out_17, out_18, out_19, out_20, out_21, out_22
endmodule

module SwitchClock (
  input  in_1,
  input  in_2,
  input  OnOff,
  output out_4
);

  wire and_1_out, and_2_out, not_1_out;

  not not_1 (not_1_out, OnOff);
  and and_1 (and_1_out, in_1, not_1_out);
  and and_2 (and_2_out, OnOff, in_2);
  or or_1 (out_4, and_1_out, and_2_out);
endmodule

module TotalSwitchClock (
  input  OnOff,
  input  Bit1,
  input  Bit2,
  input  Bit3,
  input  Bit4,
  input  SecondBit1,
  input  SecondBit2,
  input  SecondBit3,
  input  Bit1Alarm,
  input  Bit2Alarm,
  input  Bit3Alarm,
  input  Bit4Alarm,
  input  SecondBit1Alarm,
  input  SecondBit2Alarm,
  input  SecondBit3Alarm,
  output out_16,
  output out_17,
  output out_18,
  output out_19,
  output out_20,
  output out_21,
  output out_22
);

  SwitchClock switchclock_1 (.in_1(Bit1), .in_2(Bit1Alarm), .OnOff(OnOff), .out_4(out_16));
  SwitchClock switchclock_2 (.in_1(Bit2), .in_2(Bit2Alarm), .OnOff(OnOff), .out_4(out_17));
  SwitchClock switchclock_3 (.in_1(Bit3), .in_2(Bit3Alarm), .OnOff(OnOff), .out_4(out_18));
  SwitchClock switchclock_4 (.in_1(Bit4), .in_2(Bit4Alarm), .OnOff(OnOff), .out_4(out_19));
  SwitchClock switchclock_5 (.in_1(SecondBit1), .in_2(SecondBit1Alarm), .OnOff(OnOff), .out_4(out_20));
  SwitchClock switchclock_6 (.in_1(SecondBit2), .in_2(SecondBit2Alarm), .OnOff(OnOff), .out_4(out_21));
  SwitchClock switchclock_7 (.in_1(SecondBit3), .in_2(SecondBit3Alarm), .OnOff(OnOff), .out_4(out_22));
endmodule
